// Digital circuit ALU.dig as structural Verilog
module ALU (
  input  [7:0] ACin,
  input  [7:0] N,
  input  CLK,
  input  [2:0] Sel,
  output [7:0] AC,
  output [7:0] MQ
);

  wire [7:0] divisor_bits_1_p3, logical_shift_1_p3, logical_shift_2_p3, MQ0, MQ1, multiplexer_1_out,
       multiplexer_2_out, multiplicador_8bits_1_p4, nand_1_out, somador_8bits_1_p4, subtrator_8bits_1_p3,
       xor_1_out;

  // somador_8bits somador_8bits_1: pin names not known; wires that end beside it: 1'b0, ACin, N, somador_8bits_1_p4
  // subtrator_8bits subtrator_8bits_1: pin names not known; wires that end beside it: ACin, N, subtrator_8bits_1_p3
  // multiplicador_8bits multiplicador_8bits_1: pin names not known; wires that end beside it: ACin, N, MQ0, multiplicador_8bits_1_p4
  // divisor_bits divisor_bits_1: pin names not known; wires that end beside it: ACin, N, divisor_bits_1_p3, MQ1
  // logical_shift logical_shift_1: pin names not known; wires that end beside it: ACin, 1'b0, logical_shift_1_p3
  // logical_shift logical_shift_2: pin names not known; wires that end beside it: ACin, 1'b1, logical_shift_2_p3
  assign nand_1_out = ~(ACin & N);  // NAnd nand_1, 8 bits wide
  assign xor_1_out = ACin ^ N;  // XOr xor_1, 8 bits wide
  Multiplexer #(.Selector_Bits(3), .Bits(8)) multiplexer_1 (
    .sel(Sel), .in_0(somador_8bits_1_p4), .in_1(subtrator_8bits_1_p3), .in_2(multiplicador_8bits_1_p4),
    .in_3(divisor_bits_1_p3), .in_4(logical_shift_1_p3), .in_5(logical_shift_2_p3), .in_6(nand_1_out),
    .in_7(xor_1_out), .out(multiplexer_1_out));
  Multiplexer #(.Selector_Bits(3), .Bits(8)) multiplexer_2 (
    .sel(Sel), .in_0({8{1'b0}}), .in_1({8{1'b0}}), .in_2(MQ0), .in_3(MQ1), .in_4({8{1'b0}}),
    .in_5({8{1'b0}}), .in_6({8{1'b0}}), .in_7({8{1'b0}}), .out(multiplexer_2_out));
  Register #(.Bits(8)) register_1 (.D(multiplexer_1_out), .C(CLK), .en(1'b1), .Q(AC));
  Register #(.Bits(8)) register_2 (.D(multiplexer_2_out), .C(CLK), .en(1'b1), .Q(MQ));
  Seven_Seg_Hex seven_seg_hex_1 (.d(AC[7:4]), .dp(1'b0));
  Seven_Seg_Hex seven_seg_hex_2 (.d(AC[3:0]), .dp(1'b0));
  Seven_Seg_Hex seven_seg_hex_3 (.d(MQ[7:4]), .dp(1'b0));
  Seven_Seg_Hex seven_seg_hex_4 (.d(MQ[3:0]), .dp(1'b0));

  // Notes on the sheet:
  //   AC
  //   MQ
endmodule
