// Digital circuit CPU.dig as structural Verilog
module CPU (
  input  [2:0] in_1,
  output [7:0] out_2
);

  wire Clock_out;
  wire [3:0] register_1_q;
  wire [7:0] alu_1_ac;
  wire [7:4] register_1_q_2;
  wire [10:0] eepromdualport_1_d;

  Button Clock (.out(Clock_out));
  EEPROMDualPort #(.AddrBits(3), .Bits(11)) eepromdualport_1 (
    .A(in_1), .Din({11{1'b0}}), .str(1'b0), .C(Clock_out), .ld(1'b1), .D(eepromdualport_1_d));
  ALU alu_1 (
    .ACin(eepromdualport_1_d[7:0]), .N({register_1_q_2, register_1_q}), .CLK(Clock_out),
    .Sel(eepromdualport_1_d[10:8]), .AC(alu_1_ac), .MQ(out_2));
  Register #(.Bits(8)) register_1 (.D(alu_1_ac), .C(Clock_out), .en(1'b1), .Q({register_1_q_2, register_1_q}));
  Seven_Seg_Hex seven_seg_hex_1 (.d(register_1_q_2), .dp(1'b0));
  Seven_Seg_Hex seven_seg_hex_2 (.d(register_1_q), .dp(1'b0));

  // Notes on the sheet:
  //   contents of eepromdualport_1 (hex, n*v repeats v):
  //   1,104
endmodule
